# Fritzing sketch stm32f103_fritzing (saved by Fritzing 0.9.4)
breadboards: 1

parts:
  M1 = STM32F103C8T6 blue mini board
  LED1 = LED - 5mm [color="Red (633nm)" package="5 mm [THT]"]
  R1 = Resistor [tolerance=±5% resistance=220 package=THT]

nets:
  N1: M1.G, M1.GND, LED1.cathode
  N2: M1.A5, R1.Pin_1
  N3: LED1.anode, R1.Pin_0
